# Fritzing sketch schematics (saved by Fritzing 0.9.2b)
breadboards: 1

parts:
  Arduino = Arduino Uno (Rev3)
  Thermocouple = Peltier Element
  U1 = LM 358 Dual Op-Amp [package="DIP8 [THT]"]
  R1 = Resistor [tolerance=±5% resistance=100 package=THT]
  R2 = Resistor [tolerance=±5% resistance=47k package=THT]
  T1 = LM35 Temperature Sensor [package="TO92 [THT]"]
  R3 = Resistor [tolerance=±5% resistance=4.7k package=THT]
  R4 = Resistor [tolerance=±5% resistance=1k package=THT]

nets:
  N1: Arduino.A0, U1.connector0
  N2: Arduino.A5/SCL, T1.Vout
  GND: Arduino.GND, Thermocouple.pin2, U1.connector2, U1.connector3, T1.GND, R4.Pin_0
  N3: Arduino.5V, U1.connector7, R3.Pin_1
  N4: Thermocouple.pin1, R1.Pin_0
  N5: U1.connector1, R1.Pin_1, R2.Pin_0
  N6: T1.+Vs, R3.Pin_0, R4.Pin_1
